// Logisim project 8bitkitten.circ as structural Verilog: 1 circuit, main circuit main
module main (
  input  in_1,
  input  in_2,
  input  in_3,
  input  in_4,
  input  in_5,
  input  in_6,
  input  in_7,
  input  in_8,
  input  in_9,
  input  in_10,
  input  in_11,
  output out_12
);

  wire and_1_out, and_2_out, and_3_out, and_4_out, and_5_out, and_6_out, and_7_out, and_8_out, not_1_out,
       not_2_out, not_3_out;

  not not_1 (not_1_out, in_1);
  not not_2 (not_2_out, in_2);
  not not_3 (not_3_out, in_3);
  and and_1 (and_1_out, not_3_out, not_1_out, not_2_out, in_4);
  and and_2 (and_2_out, in_3, not_1_out, not_2_out, in_5);
  and and_3 (and_3_out, not_3_out, not_1_out, in_2, in_6);
  and and_4 (and_4_out, in_3, not_1_out, in_2, in_7);
  and and_5 (and_5_out, not_3_out, in_1, not_2_out, in_8);
  and and_6 (and_6_out, in_3, in_1, not_2_out, in_9);
  and and_7 (and_7_out, not_3_out, in_1, in_2, in_10);
  and and_8 (and_8_out, in_3, in_1, in_2, in_11);
  or or_1 (out_12, and_1_out, and_2_out, and_3_out, and_4_out, and_5_out, and_6_out, and_7_out, and_8_out);
endmodule
