// Logisim project main.circ as structural Verilog: 18 circuits, main circuit main
module main (
  input  in_1,
  input  in_2,
  input  in_3,
  input  in_4,
  input  in_5,
  output out_6,
  output out_7,
  output out_8,
  output out_9
);

  Multiplexer multiplexer_1 (.in0(in_2), .in1(in_3), .out(out_6), .sel(in_1));  // open: en
  Multiplexer multiplexer_2 (.in0(in_3), .in1(in_4), .out(out_7), .sel(in_1));  // open: en
  Multiplexer multiplexer_3 (.in0(in_4), .in1(in_5), .out(out_8), .sel(in_1));  // open: en
  Multiplexer multiplexer_4 (.in0(in_5), .in1(in_2), .out(out_9), .sel(in_1));  // open: en
endmodule

module multiplexer (
  input  in_1,
  input  in_2,
  input  in_3,
  input  in_4,
  input  in_5,
  input  in_6,
  input  in_7,
  input  in_8,
  input  in_9,
  input  in_10,
  input  in_11,
  output out_12
);

  wire and_1_out, and_2_out, and_3_out, and_4_out, and_5_out, and_6_out, and_7_out, and_8_out, not_1_out,
       not_2_out, not_3_out;

  not not_1 (not_1_out, in_1);
  not not_2 (not_2_out, in_2);
  not not_3 (not_3_out, in_3);
  and and_1 (and_1_out, not_3_out, not_1_out, not_2_out, in_4);
  and and_2 (and_2_out, in_3, not_1_out, not_2_out, in_5);
  and and_3 (and_3_out, not_3_out, not_1_out, in_2, in_6);
  and and_4 (and_4_out, in_3, not_1_out, in_2, in_7);
  and and_5 (and_5_out, not_3_out, in_1, not_2_out, in_8);
  and and_6 (and_6_out, in_3, in_1, not_2_out, in_9);
  and and_7 (and_7_out, not_3_out, in_1, in_2, in_10);
  and and_8 (and_8_out, in_3, in_1, in_2, in_11);
  or or_1 (out_12, and_1_out, and_2_out, and_3_out, and_4_out, and_5_out, and_6_out, and_7_out, and_8_out);
endmodule

module demultiplexer (
  input  in_1,
  input  in_2,
  input  in_3,
  input  in_4,
  output out_5,
  output out_6,
  output out_7,
  output out_8,
  output out_9,
  output out_10,
  output out_11,
  output out_12
);

  wire not_1_out, not_2_out, not_3_out;

  not not_1 (not_1_out, in_1);
  not not_2 (not_2_out, in_2);
  not not_3 (not_3_out, in_3);
  and and_1 (out_5, not_3_out, not_1_out, not_2_out, in_4);
  and and_2 (out_6, in_3, not_1_out, not_2_out, in_4);
  and and_3 (out_7, not_3_out, not_1_out, in_2, in_4);
  and and_4 (out_8, in_3, not_1_out, in_2, in_4);
  and and_5 (out_9, not_3_out, in_1, not_2_out, in_4);
  and and_6 (out_10, in_3, in_1, not_2_out, in_4);
  and and_7 (out_11, not_3_out, in_1, in_2, in_4);
  and and_8 (out_12, in_3, in_1, in_2, in_4);
endmodule

module Bit_Shifter (
  input  in_1,
  input  in_2,
  input  in_3,
  input  in_4,
  input  in_5,
  output out_6,
  output out_7,
  output out_8,
  output out_9
);

  Multiplexer multiplexer_1 (.in0(in_2), .in1(in_3), .out(out_6), .sel(in_1));  // open: en
  Multiplexer multiplexer_2 (.in0(in_3), .in1(in_4), .out(out_7), .sel(in_1));  // open: en
  Multiplexer multiplexer_3 (.in0(in_4), .in1(in_5), .out(out_8), .sel(in_1));  // open: en
  Multiplexer multiplexer_4 (.in0(in_5), .in1(in_2), .out(out_9), .sel(in_1));  // open: en
endmodule

module _8_bit_barrel_Shifter (
  input  Shift_1,
  input  Shift_2,
  input  Shift_4,
  input  Input_A,
  input  Input_B,
  input  Input_C,
  input  Input_D,
  input  Input_E,
  input  Input_F,
  input  Input_G,
  input  Input_H,
  output Output_A,
  output Output_B,
  output Output_C,
  output Output_D,
  output Output_E,
  output Output_F,
  output Output_G,
  output Output_H
);

  wire multiplexer_1_out, multiplexer_2_out, multiplexer_3_out, multiplexer_4_out, multiplexer_5_out,
       multiplexer_6_out, multiplexer_7_out, multiplexer_8_out, multiplexer_9_out, multiplexer_10_out,
       multiplexer_11_out, multiplexer_12_out, multiplexer_13_out, multiplexer_14_out, multiplexer_15_out,
       multiplexer_16_out;

  Multiplexer multiplexer_1 (.in0(Input_A), .in1(Input_B), .out(multiplexer_1_out), .sel(Shift_1));  // open: en
  Multiplexer multiplexer_2 (.in0(Input_B), .in1(Input_C), .out(multiplexer_2_out), .sel(Shift_1));  // open: en
  Multiplexer multiplexer_3 (.in0(Input_C), .in1(Input_D), .out(multiplexer_3_out), .sel(Shift_1));  // open: en
  Multiplexer multiplexer_4 (.in0(Input_D), .in1(Input_E), .out(multiplexer_4_out), .sel(Shift_1));  // open: en
  Multiplexer multiplexer_5 (.in0(Input_E), .in1(Input_F), .out(multiplexer_5_out), .sel(Shift_1));  // open: en
  Multiplexer multiplexer_6 (.in0(Input_F), .in1(Input_G), .out(multiplexer_6_out), .sel(Shift_1));  // open: en
  Multiplexer multiplexer_7 (.in0(Input_G), .in1(Input_H), .out(multiplexer_7_out), .sel(Shift_1));  // open: en
  Multiplexer multiplexer_8 (.in0(Input_H), .in1(Input_A), .out(multiplexer_8_out), .sel(Shift_1));  // open: en
  Multiplexer multiplexer_9 (
    .in0(multiplexer_1_out), .in1(multiplexer_3_out), .out(multiplexer_9_out), .sel(Shift_2));  // open: en
  Multiplexer multiplexer_10 (
    .in0(multiplexer_2_out), .in1(multiplexer_4_out), .out(multiplexer_10_out), .sel(Shift_2));  // open: en
  Multiplexer multiplexer_11 (
    .in0(multiplexer_3_out), .in1(multiplexer_5_out), .out(multiplexer_11_out), .sel(Shift_2));  // open: en
  Multiplexer multiplexer_12 (
    .in0(multiplexer_4_out), .in1(multiplexer_6_out), .out(multiplexer_12_out), .sel(Shift_2));  // open: en
  Multiplexer multiplexer_13 (
    .in0(multiplexer_5_out), .in1(multiplexer_7_out), .out(multiplexer_13_out), .sel(Shift_2));  // open: en
  Multiplexer multiplexer_14 (
    .in0(multiplexer_6_out), .in1(multiplexer_8_out), .out(multiplexer_14_out), .sel(Shift_2));  // open: en
  Multiplexer multiplexer_15 (
    .in0(multiplexer_7_out), .in1(multiplexer_1_out), .out(multiplexer_15_out), .sel(Shift_2));  // open: en
  Multiplexer multiplexer_16 (
    .in0(multiplexer_8_out), .in1(multiplexer_2_out), .out(multiplexer_16_out), .sel(Shift_2));  // open: en
  Multiplexer multiplexer_17 (
    .in0(multiplexer_9_out), .in1(multiplexer_13_out), .out(Output_A), .sel(Shift_4));  // open: en
  Multiplexer multiplexer_18 (
    .in0(multiplexer_10_out), .in1(multiplexer_14_out), .out(Output_B), .sel(Shift_4));  // open: en
  Multiplexer multiplexer_19 (
    .in0(multiplexer_11_out), .in1(multiplexer_15_out), .out(Output_C), .sel(Shift_4));  // open: en
  Multiplexer multiplexer_20 (
    .in0(multiplexer_12_out), .in1(multiplexer_16_out), .out(Output_D), .sel(Shift_4));  // open: en
  Multiplexer multiplexer_21 (
    .in0(multiplexer_13_out), .in1(multiplexer_9_out), .out(Output_E), .sel(Shift_4));  // open: en
  Multiplexer multiplexer_22 (
    .in0(multiplexer_14_out), .in1(multiplexer_10_out), .out(Output_F), .sel(Shift_4));  // open: en
  Multiplexer multiplexer_23 (
    .in0(multiplexer_15_out), .in1(multiplexer_11_out), .out(Output_G), .sel(Shift_4));  // open: en
  Multiplexer multiplexer_24 (
    .in0(multiplexer_16_out), .in1(multiplexer_12_out), .out(Output_H), .sel(Shift_4));  // open: en
endmodule

module _4bit_ALU (
  input  Select_1,
  input  Select_2,
  input  Invert_A,
  input  Invert_B,
  input  A1,
  input  B1,
  input  A2,
  input  B2,
  input  A3,
  input  B3,
  input  A4,
  input  B4,
  output Output_A,
  output Output_B,
  output Output_C,
  output Output_D
);

  wire and_1_out, and_2_out, and_3_out, and_4_out, full_adder_1_carry_out, full_adder_1_out,
       full_adder_2_carry_out, full_adder_2_out, full_adder_3_carry_out, full_adder_3_out, full_adder_4_out,
       n2_bit_multiplexer_1_out, n2_bit_multiplexer_1_select_out, n2_bit_multiplexer_2_out,
       n2_bit_multiplexer_2_select_out, n2_bit_multiplexer_3_out, n2_bit_multiplexer_3_select_out,
       n2_bit_multiplexer_4_out, n2_bit_multiplexer_5_out, n2_bit_multiplexer_5_select_out,
       n2_bit_multiplexer_6_out, n2_bit_multiplexer_6_select_out, n2_bit_multiplexer_7_out,
       n2_bit_multiplexer_7_select_out, n2_bit_multiplexer_8_out, n2_bit_multiplexer_8_select_out,
       n4_bit_barrel_shifter_1_out_a, n4_bit_barrel_shifter_1_out_b, n4_bit_barrel_shifter_1_out_c,
       n4_bit_barrel_shifter_1_out_d, n4_bit_multiplexer_1_select_1_out, n4_bit_multiplexer_1_select_2_out,
       n4_bit_multiplexer_2_select_1_out, n4_bit_multiplexer_2_select_2_out,
       n4_bit_multiplexer_3_select_1_out, n4_bit_multiplexer_3_select_2_out, not_1_out, not_2_out, not_3_out,
       not_4_out, not_5_out, not_6_out, not_7_out, not_8_out, or_1_out, or_2_out, or_3_out, or_4_out;

  _2_bit_multiplexer u_2_bit_multiplexer_1 (
    .A(A1), .B(not_1_out), .Select(Invert_A), .Select_Out(n2_bit_multiplexer_1_select_out),
    .Out(n2_bit_multiplexer_1_out));
  not not_1 (not_1_out, A1);
  _2_bit_multiplexer u_2_bit_multiplexer_2 (
    .A(A2), .B(not_2_out), .Select(n2_bit_multiplexer_1_select_out),
    .Select_Out(n2_bit_multiplexer_2_select_out), .Out(n2_bit_multiplexer_2_out));
  not not_2 (not_2_out, A2);
  _2_bit_multiplexer u_2_bit_multiplexer_3 (
    .A(A3), .B(not_3_out), .Select(n2_bit_multiplexer_2_select_out),
    .Select_Out(n2_bit_multiplexer_3_select_out), .Out(n2_bit_multiplexer_3_out));
  not not_3 (not_3_out, A3);
  _2_bit_multiplexer u_2_bit_multiplexer_4 (
    .A(A4), .B(not_4_out), .Select(n2_bit_multiplexer_3_select_out), .Out(n2_bit_multiplexer_4_out));  // open: Select_Out
  not not_4 (not_4_out, A4);
  _2_bit_multiplexer u_2_bit_multiplexer_5 (
    .A(B1), .B(not_5_out), .Select(Invert_B), .Select_Out(n2_bit_multiplexer_5_select_out),
    .Out(n2_bit_multiplexer_5_out));
  not not_5 (not_5_out, B1);
  _2_bit_multiplexer u_2_bit_multiplexer_6 (
    .A(B2), .B(not_6_out), .Select(n2_bit_multiplexer_5_select_out),
    .Select_Out(n2_bit_multiplexer_6_select_out), .Out(n2_bit_multiplexer_6_out));
  not not_6 (not_6_out, B2);
  _2_bit_multiplexer u_2_bit_multiplexer_7 (
    .A(B3), .B(not_7_out), .Select(n2_bit_multiplexer_6_select_out),
    .Select_Out(n2_bit_multiplexer_7_select_out), .Out(n2_bit_multiplexer_7_out));
  not not_7 (not_7_out, B3);
  _2_bit_multiplexer u_2_bit_multiplexer_8 (
    .A(B4), .B(not_8_out), .Select(n2_bit_multiplexer_7_select_out),
    .Select_Out(n2_bit_multiplexer_8_select_out), .Out(n2_bit_multiplexer_8_out));
  not not_8 (not_8_out, B4);
  Full_Adder full_adder_1 (
    .Carry_in(n2_bit_multiplexer_8_select_out), .A(n2_bit_multiplexer_1_out), .B(n2_bit_multiplexer_5_out),
    .Out(full_adder_1_out), .Carry_Out(full_adder_1_carry_out));
  Full_Adder full_adder_2 (
    .Carry_in(full_adder_1_carry_out), .A(n2_bit_multiplexer_2_out), .B(n2_bit_multiplexer_6_out),
    .Out(full_adder_2_out), .Carry_Out(full_adder_2_carry_out));
  Full_Adder full_adder_3 (
    .Carry_in(full_adder_2_carry_out), .A(n2_bit_multiplexer_3_out), .B(n2_bit_multiplexer_7_out),
    .Out(full_adder_3_out), .Carry_Out(full_adder_3_carry_out));
  Full_Adder full_adder_4 (
    .Carry_in(full_adder_3_carry_out), .A(n2_bit_multiplexer_4_out), .B(n2_bit_multiplexer_8_out),
    .Out(full_adder_4_out));  // open: Carry_Out
  _4_bit_barrel_shifter u_4_bit_barrel_shifter_1 (
    .A_input(n2_bit_multiplexer_1_out), .B_input(n2_bit_multiplexer_2_out),
    .C_input(n2_bit_multiplexer_3_out), .D_input(n2_bit_multiplexer_4_out),
    .Out_A(n4_bit_barrel_shifter_1_out_a), .Out_B(n4_bit_barrel_shifter_1_out_b),
    .Out_C(n4_bit_barrel_shifter_1_out_c), .Out_D(n4_bit_barrel_shifter_1_out_d),
    .Shift_A(n2_bit_multiplexer_5_out), .Shift_B(n2_bit_multiplexer_6_out));
  and and_1 (and_1_out, n2_bit_multiplexer_1_out, n2_bit_multiplexer_5_out);
  and and_2 (and_2_out, n2_bit_multiplexer_2_out, n2_bit_multiplexer_6_out);
  and and_3 (and_3_out, n2_bit_multiplexer_3_out, n2_bit_multiplexer_7_out);
  and and_4 (and_4_out, n2_bit_multiplexer_4_out, n2_bit_multiplexer_8_out);
  or or_1 (or_1_out, n2_bit_multiplexer_1_out, n2_bit_multiplexer_5_out);
  or or_2 (or_2_out, n2_bit_multiplexer_2_out, n2_bit_multiplexer_6_out);
  or or_3 (or_3_out, n2_bit_multiplexer_3_out, n2_bit_multiplexer_7_out);
  or or_4 (or_4_out, n2_bit_multiplexer_4_out, n2_bit_multiplexer_8_out);
  _4_bit_multiplexer u_4_bit_multiplexer_1 (
    .A_input(n4_bit_barrel_shifter_1_out_a), .B_input(and_1_out), .C_input(or_1_out),
    .D_input(full_adder_1_out), .Select_1(Select_1), .Select_2(Select_2),
    .Select_1_Out(n4_bit_multiplexer_1_select_1_out), .Select_2_Out(n4_bit_multiplexer_1_select_2_out),
    .Output(Output_A));
  _4_bit_multiplexer u_4_bit_multiplexer_2 (
    .A_input(n4_bit_barrel_shifter_1_out_b), .B_input(and_2_out), .C_input(or_2_out),
    .D_input(full_adder_2_out), .Select_1(n4_bit_multiplexer_1_select_1_out),
    .Select_2(n4_bit_multiplexer_1_select_2_out), .Select_1_Out(n4_bit_multiplexer_2_select_1_out),
    .Select_2_Out(n4_bit_multiplexer_2_select_2_out), .Output(Output_B));
  _4_bit_multiplexer u_4_bit_multiplexer_3 (
    .A_input(n4_bit_barrel_shifter_1_out_c), .B_input(and_3_out), .C_input(or_3_out),
    .D_input(full_adder_3_out), .Select_1(n4_bit_multiplexer_2_select_1_out),
    .Select_2(n4_bit_multiplexer_2_select_2_out), .Select_1_Out(n4_bit_multiplexer_3_select_1_out),
    .Select_2_Out(n4_bit_multiplexer_3_select_2_out), .Output(Output_C));
  _4_bit_multiplexer u_4_bit_multiplexer_4 (
    .A_input(n4_bit_barrel_shifter_1_out_d), .B_input(and_4_out), .C_input(or_4_out),
    .D_input(full_adder_4_out), .Select_1(n4_bit_multiplexer_3_select_1_out),
    .Select_2(n4_bit_multiplexer_3_select_2_out), .Output(Output_D));  // open: Select_1_Out, Select_2_Out

  // Notes on the sheet:
  //   1 0 - or
  //   0 1 - and
  //   Is the shifter shifting in the right direction?
  //   0 0 - Bit shifting
  //   11 - add
endmodule

module Full_Adder (
  input  Carry_in,
  input  A,
  input  B,
  output Out,
  output Carry_Out
);

  wire and_1_out, and_2_out, xor_1_out;

  and and_1 (and_1_out, B, A);
  xor xor_1 (xor_1_out, A, B);
  xor xor_2 (Out, Carry_in, xor_1_out);
  and and_2 (and_2_out, Carry_in, xor_1_out);
  or or_1 (Carry_Out, and_2_out, and_1_out);
endmodule

module _2_bit_multiplexer (
  input  Select,
  input  A,
  input  B,
  output Out,
  output Select_Out
);

  wire and_1_out, and_2_out, not_1_out;

  not not_1 (not_1_out, Select);
  and and_1 (and_1_out, not_1_out, A);
  and and_2 (and_2_out, Select, B);
  or or_1 (Out, and_1_out, and_2_out);

  assign Select_Out = Select;
endmodule

module _4_bit_multiplexer (
  input  Select_1,
  input  Select_2,
  input  A_input,
  input  B_input,
  input  C_input,
  input  D_input,
  output Output,
  output Select_1_Out,
  output Select_2_Out
);

  wire and_1_out, and_2_out, and_3_out, and_4_out, not_1_out, not_2_out;

  not not_1 (not_1_out, Select_1);
  not not_2 (not_2_out, Select_2);
  and and_1 (and_1_out, not_2_out, not_1_out, A_input);
  and and_2 (and_2_out, Select_2, not_1_out, B_input);
  and and_3 (and_3_out, not_2_out, Select_1, C_input);
  and and_4 (and_4_out, Select_2, Select_1, D_input);
  or or_1 (Output, and_1_out, and_2_out, and_3_out, and_4_out);

  assign Select_1_Out = Select_1;
  assign Select_2_Out = Select_2;
endmodule

module _4_bit_barrel_shifter (
  input  Shift_A,
  input  Shift_B,
  input  A_input,
  input  B_input,
  input  C_input,
  input  D_input,
  output Out_A,
  output Out_B,
  output Out_C,
  output Out_D
);

  wire multiplexer_1_out, multiplexer_2_out, multiplexer_3_out, multiplexer_4_out;

  Multiplexer multiplexer_1 (.in0(A_input), .in1(B_input), .out(multiplexer_1_out), .sel(Shift_A));  // open: en
  Multiplexer multiplexer_2 (.in0(B_input), .in1(C_input), .out(multiplexer_2_out), .sel(Shift_A));  // open: en
  Multiplexer multiplexer_3 (.in0(C_input), .in1(D_input), .out(multiplexer_3_out), .sel(Shift_A));  // open: en
  Multiplexer multiplexer_4 (.in0(D_input), .in1(A_input), .out(multiplexer_4_out), .sel(Shift_A));  // open: en
  Multiplexer multiplexer_5 (.in0(multiplexer_1_out), .in1(multiplexer_3_out), .out(Out_A), .sel(Shift_B));  // open: en
  Multiplexer multiplexer_6 (.in0(multiplexer_2_out), .in1(multiplexer_4_out), .out(Out_B), .sel(Shift_B));  // open: en
  Multiplexer multiplexer_7 (.in0(multiplexer_3_out), .in1(multiplexer_1_out), .out(Out_C), .sel(Shift_B));  // open: en
  Multiplexer multiplexer_8 (.in0(multiplexer_4_out), .in1(multiplexer_2_out), .out(Out_D), .sel(Shift_B));  // open: en
endmodule

module _8bit_ALU (
  input  Select_1,
  input  Select_2,
  input  Invert_A,
  input  Invert_B,
  input  A1,
  input  B1,
  input  A2,
  input  B2,
  input  A3,
  input  B3,
  input  A4,
  input  B4,
  input  A5,
  input  B5,
  input  A6,
  input  B6,
  input  A7,
  input  B7,
  input  A8,
  input  B8,
  output Output_A,
  output Output_B,
  output [7:0] _8bit_output,
  output Output_C,
  output Output_D,
  output Output_A_2,
  output Output_B_2,
  output Output_C_2,
  output Output_D_2,
  output Adder_Carry_Out
);

  wire _1_2_out, _1_3_out, _1_4_select_1_out, _1_4_select_2_out, _1_carry_out, _1_out, _2_2_out, _2_3_out,
       _2_4_select_1_out, _2_4_select_2_out, _2_carry_out, _2_out, _3_2_out, _3_3_out, _3_4_select_1_out,
       _3_4_select_2_out, _3_carry_out, _3_out, _4_2_out, _4_3_out, _4_4_select_1_out, _4_4_select_2_out,
       _4_carry_out, _4_out, _5_2_out, _5_3_out, _5_4_select_1_out, _5_4_select_2_out, _5_carry_out, _5_out,
       _6_2_out, _6_3_out, _6_4_select_1_out, _6_4_select_2_out, _6_carry_out, _6_out, _7_2_out, _7_3_out,
       _7_4_select_1_out, _7_4_select_2_out, _7_carry_out, _7_out, _8_2_out, _8_3_out, _8_out,
       n2_bit_multiplexer_1_out, n2_bit_multiplexer_1_select_out, n2_bit_multiplexer_2_out,
       n2_bit_multiplexer_2_select_out, n2_bit_multiplexer_3_out, n2_bit_multiplexer_3_select_out,
       n2_bit_multiplexer_4_out, n2_bit_multiplexer_4_select_out, n2_bit_multiplexer_5_out,
       n2_bit_multiplexer_5_select_out, n2_bit_multiplexer_6_out, n2_bit_multiplexer_6_select_out,
       n2_bit_multiplexer_7_out, n2_bit_multiplexer_7_select_out, n2_bit_multiplexer_8_out,
       n2_bit_multiplexer_9_out, n2_bit_multiplexer_9_select_out, n2_bit_multiplexer_10_out,
       n2_bit_multiplexer_10_select_out, n2_bit_multiplexer_11_out, n2_bit_multiplexer_11_select_out,
       n2_bit_multiplexer_12_out, n2_bit_multiplexer_12_select_out, n2_bit_multiplexer_13_out,
       n2_bit_multiplexer_13_select_out, n2_bit_multiplexer_14_out, n2_bit_multiplexer_14_select_out,
       n2_bit_multiplexer_15_out, n2_bit_multiplexer_15_select_out, n2_bit_multiplexer_16_out,
       n8_bit_barrel_shifter_1_output_a, n8_bit_barrel_shifter_1_output_b, n8_bit_barrel_shifter_1_output_c,
       n8_bit_barrel_shifter_1_output_d, n8_bit_barrel_shifter_1_output_e, n8_bit_barrel_shifter_1_output_f,
       n8_bit_barrel_shifter_1_output_g, n8_bit_barrel_shifter_1_output_h, not_1_out, not_2_out, not_3_out,
       not_4_out, not_5_out, not_6_out, not_7_out, not_8_out, not_9_out, not_10_out, not_11_out, not_12_out,
       not_13_out, not_14_out, not_15_out, not_16_out;

  not not_1 (not_1_out, A1);
  not not_2 (not_2_out, A2);
  not not_3 (not_3_out, A3);
  not not_4 (not_4_out, A4);
  not not_5 (not_5_out, A5);
  not not_6 (not_6_out, A6);
  not not_7 (not_7_out, A7);
  not not_8 (not_8_out, A8);
  _2_bit_multiplexer u_2_bit_multiplexer_1 (
    .A(A1), .B(not_1_out), .Select(Invert_A), .Select_Out(n2_bit_multiplexer_1_select_out),
    .Out(n2_bit_multiplexer_1_out));
  _2_bit_multiplexer u_2_bit_multiplexer_2 (
    .A(A2), .B(not_2_out), .Select(n2_bit_multiplexer_1_select_out),
    .Select_Out(n2_bit_multiplexer_2_select_out), .Out(n2_bit_multiplexer_2_out));
  _2_bit_multiplexer u_2_bit_multiplexer_3 (
    .A(A3), .B(not_3_out), .Select(n2_bit_multiplexer_2_select_out),
    .Select_Out(n2_bit_multiplexer_3_select_out), .Out(n2_bit_multiplexer_3_out));
  _2_bit_multiplexer u_2_bit_multiplexer_4 (
    .A(A4), .B(not_4_out), .Select(n2_bit_multiplexer_3_select_out),
    .Select_Out(n2_bit_multiplexer_4_select_out), .Out(n2_bit_multiplexer_4_out));
  _2_bit_multiplexer u_2_bit_multiplexer_5 (
    .A(A5), .B(not_5_out), .Select(n2_bit_multiplexer_4_select_out),
    .Select_Out(n2_bit_multiplexer_5_select_out), .Out(n2_bit_multiplexer_5_out));
  _2_bit_multiplexer u_2_bit_multiplexer_6 (
    .A(A6), .B(not_6_out), .Select(n2_bit_multiplexer_5_select_out),
    .Select_Out(n2_bit_multiplexer_6_select_out), .Out(n2_bit_multiplexer_6_out));
  _2_bit_multiplexer u_2_bit_multiplexer_7 (
    .A(A7), .B(not_7_out), .Select(n2_bit_multiplexer_6_select_out),
    .Select_Out(n2_bit_multiplexer_7_select_out), .Out(n2_bit_multiplexer_7_out));
  _2_bit_multiplexer u_2_bit_multiplexer_8 (
    .A(A8), .B(not_8_out), .Select(n2_bit_multiplexer_7_select_out), .Out(n2_bit_multiplexer_8_out));  // open: Select_Out
  _2_bit_multiplexer u_2_bit_multiplexer_9 (
    .A(B1), .B(not_9_out), .Select(Invert_B), .Select_Out(n2_bit_multiplexer_9_select_out),
    .Out(n2_bit_multiplexer_9_out));
  not not_9 (not_9_out, B1);
  _2_bit_multiplexer u_2_bit_multiplexer_10 (
    .A(B2), .B(not_10_out), .Select(n2_bit_multiplexer_9_select_out),
    .Select_Out(n2_bit_multiplexer_10_select_out), .Out(n2_bit_multiplexer_10_out));
  not not_10 (not_10_out, B2);
  _2_bit_multiplexer u_2_bit_multiplexer_11 (
    .A(B3), .B(not_11_out), .Select(n2_bit_multiplexer_10_select_out),
    .Select_Out(n2_bit_multiplexer_11_select_out), .Out(n2_bit_multiplexer_11_out));
  not not_11 (not_11_out, B3);
  _2_bit_multiplexer u_2_bit_multiplexer_12 (
    .A(B4), .B(not_12_out), .Select(n2_bit_multiplexer_11_select_out),
    .Select_Out(n2_bit_multiplexer_12_select_out), .Out(n2_bit_multiplexer_12_out));
  not not_12 (not_12_out, B4);
  _2_bit_multiplexer u_2_bit_multiplexer_13 (
    .A(B5), .B(not_13_out), .Select(n2_bit_multiplexer_12_select_out),
    .Select_Out(n2_bit_multiplexer_13_select_out), .Out(n2_bit_multiplexer_13_out));
  not not_13 (not_13_out, B5);
  _2_bit_multiplexer u_2_bit_multiplexer_14 (
    .A(B6), .B(not_14_out), .Select(n2_bit_multiplexer_13_select_out),
    .Select_Out(n2_bit_multiplexer_14_select_out), .Out(n2_bit_multiplexer_14_out));
  not not_14 (not_14_out, B6);
  _2_bit_multiplexer u_2_bit_multiplexer_15 (
    .A(B7), .B(not_15_out), .Select(n2_bit_multiplexer_14_select_out),
    .Select_Out(n2_bit_multiplexer_15_select_out), .Out(n2_bit_multiplexer_15_out));
  not not_15 (not_15_out, B7);
  _2_bit_multiplexer u_2_bit_multiplexer_16 (
    .A(B8), .B(not_16_out), .Select(n2_bit_multiplexer_15_select_out), .Out(n2_bit_multiplexer_16_out));  // open: Select_Out
  not not_16 (not_16_out, B8);
  Full_Adder _1 (
    .Carry_in(n2_bit_multiplexer_14_select_out), .A(n2_bit_multiplexer_1_out), .B(n2_bit_multiplexer_9_out),
    .Out(_1_out), .Carry_Out(_1_carry_out));
  Full_Adder _2 (
    .Carry_in(_1_carry_out), .A(n2_bit_multiplexer_2_out), .B(n2_bit_multiplexer_10_out), .Out(_2_out),
    .Carry_Out(_2_carry_out));
  Full_Adder _3 (
    .Carry_in(_2_carry_out), .A(n2_bit_multiplexer_3_out), .B(n2_bit_multiplexer_11_out), .Out(_3_out),
    .Carry_Out(_3_carry_out));
  Full_Adder _4 (
    .Carry_in(_3_carry_out), .A(n2_bit_multiplexer_4_out), .B(n2_bit_multiplexer_12_out), .Out(_4_out),
    .Carry_Out(_4_carry_out));
  Full_Adder _5 (
    .Carry_in(_4_carry_out), .A(n2_bit_multiplexer_5_out), .B(n2_bit_multiplexer_13_out), .Out(_5_out),
    .Carry_Out(_5_carry_out));
  Full_Adder _6 (
    .Carry_in(_5_carry_out), .A(n2_bit_multiplexer_6_out), .B(n2_bit_multiplexer_14_out), .Out(_6_out),
    .Carry_Out(_6_carry_out));
  Full_Adder _7 (
    .Carry_in(_6_carry_out), .A(n2_bit_multiplexer_7_out), .B(n2_bit_multiplexer_15_out), .Out(_7_out),
    .Carry_Out(_7_carry_out));
  Full_Adder _8 (
    .Carry_in(_7_carry_out), .A(n2_bit_multiplexer_8_out), .B(n2_bit_multiplexer_16_out), .Out(_8_out),
    .Carry_Out(Adder_Carry_Out));
  _8_bit_barrel_Shifter u_8_bit_barrel_shifter_1 (
    .Input_A(n2_bit_multiplexer_1_out), .Input_B(n2_bit_multiplexer_2_out),
    .Input_C(n2_bit_multiplexer_3_out), .Input_D(n2_bit_multiplexer_4_out),
    .Input_E(n2_bit_multiplexer_5_out), .Input_F(n2_bit_multiplexer_6_out),
    .Input_G(n2_bit_multiplexer_7_out), .Input_H(n2_bit_multiplexer_8_out),
    .Shift_1(n2_bit_multiplexer_9_out), .Shift_2(n2_bit_multiplexer_10_out),
    .Shift_4(n2_bit_multiplexer_11_out), .Output_A(n8_bit_barrel_shifter_1_output_a),
    .Output_B(n8_bit_barrel_shifter_1_output_b), .Output_C(n8_bit_barrel_shifter_1_output_c),
    .Output_D(n8_bit_barrel_shifter_1_output_d), .Output_E(n8_bit_barrel_shifter_1_output_e),
    .Output_F(n8_bit_barrel_shifter_1_output_f), .Output_G(n8_bit_barrel_shifter_1_output_g),
    .Output_H(n8_bit_barrel_shifter_1_output_h));
  and _1_2 (_1_2_out, n2_bit_multiplexer_1_out, n2_bit_multiplexer_9_out);
  and _2_2 (_2_2_out, n2_bit_multiplexer_2_out, n2_bit_multiplexer_10_out);
  and _3_2 (_3_2_out, n2_bit_multiplexer_3_out, n2_bit_multiplexer_11_out);
  and _4_2 (_4_2_out, n2_bit_multiplexer_4_out, n2_bit_multiplexer_12_out);
  and _5_2 (_5_2_out, n2_bit_multiplexer_5_out, n2_bit_multiplexer_13_out);
  and _6_2 (_6_2_out, n2_bit_multiplexer_6_out, n2_bit_multiplexer_14_out);
  and _7_2 (_7_2_out, n2_bit_multiplexer_7_out, n2_bit_multiplexer_15_out);
  and _8_2 (_8_2_out, n2_bit_multiplexer_8_out, n2_bit_multiplexer_16_out);
  or _1_3 (_1_3_out, n2_bit_multiplexer_1_out, n2_bit_multiplexer_9_out);
  or _2_3 (_2_3_out, n2_bit_multiplexer_2_out, n2_bit_multiplexer_10_out);
  or _3_3 (_3_3_out, n2_bit_multiplexer_3_out, n2_bit_multiplexer_11_out);
  or _4_3 (_4_3_out, n2_bit_multiplexer_4_out, n2_bit_multiplexer_12_out);
  or _5_3 (_5_3_out, n2_bit_multiplexer_5_out, n2_bit_multiplexer_13_out);
  or _6_3 (_6_3_out, n2_bit_multiplexer_6_out, n2_bit_multiplexer_14_out);
  or _7_3 (_7_3_out, n2_bit_multiplexer_7_out, n2_bit_multiplexer_15_out);
  or _8_3 (_8_3_out, n2_bit_multiplexer_8_out, n2_bit_multiplexer_16_out);
  _4_bit_multiplexer _1_4 (
    .A_input(n8_bit_barrel_shifter_1_output_a), .B_input(_1_2_out), .C_input(_1_3_out), .D_input(_1_out),
    .Select_1(Select_1), .Select_2(Select_2), .Select_1_Out(_1_4_select_1_out),
    .Select_2_Out(_1_4_select_2_out), .Output(_8bit_output[0]));
  _4_bit_multiplexer _2_4 (
    .A_input(n8_bit_barrel_shifter_1_output_b), .B_input(_2_2_out), .C_input(_2_3_out), .D_input(_2_out),
    .Select_1(_1_4_select_1_out), .Select_2(_1_4_select_2_out), .Select_1_Out(_2_4_select_1_out),
    .Select_2_Out(_2_4_select_2_out), .Output(_8bit_output[1]));
  _4_bit_multiplexer _3_4 (
    .A_input(n8_bit_barrel_shifter_1_output_c), .B_input(_3_2_out), .C_input(_3_3_out), .D_input(_3_out),
    .Select_1(_2_4_select_1_out), .Select_2(_2_4_select_2_out), .Select_1_Out(_3_4_select_1_out),
    .Select_2_Out(_3_4_select_2_out), .Output(_8bit_output[2]));
  _4_bit_multiplexer _4_4 (
    .A_input(n8_bit_barrel_shifter_1_output_d), .B_input(_4_2_out), .C_input(_4_3_out), .D_input(_4_out),
    .Select_1(_3_4_select_1_out), .Select_2(_3_4_select_2_out), .Select_1_Out(_4_4_select_1_out),
    .Select_2_Out(_4_4_select_2_out), .Output(_8bit_output[3]));
  _4_bit_multiplexer _5_4 (
    .A_input(n8_bit_barrel_shifter_1_output_e), .B_input(_5_2_out), .C_input(_5_3_out), .D_input(_5_out),
    .Select_1(_4_4_select_1_out), .Select_2(_4_4_select_2_out), .Select_1_Out(_5_4_select_1_out),
    .Select_2_Out(_5_4_select_2_out), .Output(_8bit_output[4]));
  _4_bit_multiplexer _6_4 (
    .A_input(n8_bit_barrel_shifter_1_output_f), .B_input(_6_2_out), .C_input(_6_3_out), .D_input(_6_out),
    .Select_1(_5_4_select_1_out), .Select_2(_5_4_select_2_out), .Select_1_Out(_6_4_select_1_out),
    .Select_2_Out(_6_4_select_2_out), .Output(_8bit_output[5]));
  _4_bit_multiplexer _7_4 (
    .A_input(n8_bit_barrel_shifter_1_output_g), .B_input(_7_2_out), .C_input(_7_3_out), .D_input(_7_out),
    .Select_1(_6_4_select_1_out), .Select_2(_6_4_select_2_out), .Select_1_Out(_7_4_select_1_out),
    .Select_2_Out(_7_4_select_2_out), .Output(_8bit_output[6]));
  _4_bit_multiplexer _8_4 (
    .A_input(n8_bit_barrel_shifter_1_output_h), .B_input(_8_2_out), .C_input(_8_3_out), .D_input(_8_out),
    .Select_1(_7_4_select_1_out), .Select_2(_7_4_select_2_out), .Output(_8bit_output[7]));  // open: Select_1_Out, Select_2_Out

  assign Output_A = _8bit_output[0];
  assign Output_A_2 = _8bit_output[4];
  assign Output_B = _8bit_output[1];
  assign Output_B_2 = _8bit_output[5];
  assign Output_C = _8bit_output[2];
  assign Output_C_2 = _8bit_output[6];
  assign Output_D = _8bit_output[3];
  assign Output_D_2 = _8bit_output[7];

  // Notes on the sheet:
  //   Negate AB on or for nand
  //   Negate AB on and for nor
  //   0 0 - Bit shifting
  //   0 1 - and
  //   1 0 - or
  //   11 - add
endmodule

module Syncronized_Latch (
  input  in_1,
  input  in_2,
  output out_3,
  output out_4
);

  wire nand_1_out, nand_2_out, Sync_out;

  Button Sync (.out(Sync_out));
  nand nand_1 (nand_1_out, in_1, Sync_out);
  nand nand_2 (nand_2_out, Sync_out, in_2);
  nand nand_3 (out_3, nand_1_out, out_4);
  nand nand_4 (out_4, out_3, nand_2_out);

  // Notes on the sheet:
  //   Button sets output to input, unless input double True
endmodule

module D_type_flip_flop (
  input  Input,
  input  Sync,
  output Output,
  output Inverted_Output
);

  wire nand_1_out, nand_2_out, nand_3_out;

  nand nand_1 (nand_1_out, Input, Input);
  nand nand_2 (nand_2_out, Input, Sync);
  nand nand_3 (nand_3_out, Sync, nand_1_out);
  nand nand_4 (Output, nand_2_out, Inverted_Output);
  nand nand_5 (Inverted_Output, Output, nand_3_out);
endmodule

module _8bit_Ram (
  input  Sync,
  input  [7:0] Input,
  output [7:0] Output
);

  D_type_flip_flop d_type_flip_flop_1 (.Input(Input[0]), .Sync(Sync), .Output(Output[0]));  // open: Inverted_Output
  D_type_flip_flop d_type_flip_flop_2 (.Input(Input[1]), .Sync(Sync), .Output(Output[1]));  // open: Inverted_Output
  D_type_flip_flop d_type_flip_flop_3 (.Input(Input[2]), .Sync(Sync), .Output(Output[2]));  // open: Inverted_Output
  D_type_flip_flop d_type_flip_flop_4 (.Input(Input[3]), .Sync(Sync), .Output(Output[3]));  // open: Inverted_Output
  D_type_flip_flop d_type_flip_flop_5 (.Input(Input[4]), .Sync(Sync), .Output(Output[4]));  // open: Inverted_Output
  D_type_flip_flop d_type_flip_flop_6 (.Input(Input[5]), .Sync(Sync), .Output(Output[5]));  // open: Inverted_Output
  D_type_flip_flop d_type_flip_flop_7 (.Input(Input[6]), .Sync(Sync), .Output(Output[6]));  // open: Inverted_Output
  D_type_flip_flop d_type_flip_flop_8 (.Input(Input[7]), .Sync(Sync), .Output(Output[7]));  // open: Inverted_Output
endmodule

module _8Bit_Register_Bank (
  input  [7:0] Input,
  input  [2:0] Demux_Select,
  input  Sync,
  input  [2:0] Multiplexer_Select,
  output [7:0] Output
);

  wire demultiplexer_1_out_5, demultiplexer_1_out_6, demultiplexer_1_out_7, demultiplexer_1_out_8,
       demultiplexer_1_out_9, demultiplexer_1_out_10, demultiplexer_1_out_11, demultiplexer_1_out_12;
  wire [7:0] n8bit_ram_1_output, n8bit_ram_2_output, n8bit_ram_3_output, n8bit_ram_4_output,
       n8bit_ram_5_output, n8bit_ram_6_output, n8bit_ram_7_output, n8bit_ram_8_output;

  demultiplexer demultiplexer_1 (
    .in_4(Sync), .in_1(Demux_Select[2]), .in_2(Demux_Select[1]), .in_3(Demux_Select[0]),
    .out_5(demultiplexer_1_out_5), .out_6(demultiplexer_1_out_6), .out_7(demultiplexer_1_out_7),
    .out_8(demultiplexer_1_out_8), .out_9(demultiplexer_1_out_9), .out_10(demultiplexer_1_out_10),
    .out_11(demultiplexer_1_out_11), .out_12(demultiplexer_1_out_12));
  _8bit_Ram u_8bit_ram_1 (.Input(Input), .Sync(demultiplexer_1_out_5), .Output(n8bit_ram_1_output));
  _8bit_Ram u_8bit_ram_2 (.Input(Input), .Sync(demultiplexer_1_out_6), .Output(n8bit_ram_2_output));
  _8bit_Ram u_8bit_ram_3 (.Input(Input), .Sync(demultiplexer_1_out_7), .Output(n8bit_ram_3_output));
  _8bit_Ram u_8bit_ram_4 (.Input(Input), .Sync(demultiplexer_1_out_8), .Output(n8bit_ram_4_output));
  _8bit_Ram u_8bit_ram_5 (.Input(Input), .Sync(demultiplexer_1_out_9), .Output(n8bit_ram_5_output));
  _8bit_Ram u_8bit_ram_6 (.Input(Input), .Sync(demultiplexer_1_out_10), .Output(n8bit_ram_6_output));
  _8bit_Ram u_8bit_ram_7 (.Input(Input), .Sync(demultiplexer_1_out_11), .Output(n8bit_ram_7_output));
  _8bit_Ram u_8bit_ram_8 (.Input(Input), .Sync(demultiplexer_1_out_12), .Output(n8bit_ram_8_output));
  Multiplexer #(.select(3), .width(8)) multiplexer_1 (
    .in0(n8bit_ram_1_output), .in1(n8bit_ram_2_output), .in2(n8bit_ram_3_output), .in3(n8bit_ram_4_output),
    .in4(n8bit_ram_5_output), .in5(n8bit_ram_6_output), .in6(n8bit_ram_7_output), .in7(n8bit_ram_8_output),
    .out(Output), .sel(Multiplexer_Select));  // open: en
endmodule

module _8bit_demux (
  input  in_1,
  input  in_2,
  input  in_3,
  input  [7:0] in_4,
  output [7:0] out_5,
  output [7:0] out_6,
  output [7:0] out_7,
  output [7:0] out_8,
  output [7:0] out_9,
  output [7:0] out_10,
  output [7:0] out_11,
  output [7:0] out_12
);

  wire [7:0] not_1_out, not_2_out, not_3_out;

  assign not_1_out = ~{8{in_1}};  // NOT_Gate not_1, 8 bits wide
  assign not_2_out = ~{8{in_2}};  // NOT_Gate not_2, 8 bits wide
  assign not_3_out = ~{8{in_3}};  // NOT_Gate not_3, 8 bits wide
  assign out_5 = not_3_out & not_1_out & not_2_out & in_4;  // AND_Gate and_1, 8 bits wide
  assign out_6 = {8{in_3}} & not_1_out & not_2_out & in_4;  // AND_Gate and_2, 8 bits wide
  assign out_7 = not_3_out & not_1_out & {8{in_2}} & in_4;  // AND_Gate and_3, 8 bits wide
  assign out_8 = {8{in_3}} & not_1_out & {8{in_2}} & in_4;  // AND_Gate and_4, 8 bits wide
  assign out_9 = not_3_out & {8{in_1}} & not_2_out & in_4;  // AND_Gate and_5, 8 bits wide
  assign out_10 = {8{in_3}} & {8{in_1}} & not_2_out & in_4;  // AND_Gate and_6, 8 bits wide
  assign out_11 = not_3_out & {8{in_1}} & {8{in_2}} & in_4;  // AND_Gate and_7, 8 bits wide
  assign out_12 = {8{in_3}} & {8{in_1}} & {8{in_2}} & in_4;  // AND_Gate and_8, 8 bits wide
endmodule

module _8bit_CPU (
  input  Invert_A,
  input  Invert_B,
  input  Select_1,
  input  Select_2,
  input  [7:0] in_5,
  input  [7:0] in_6,
  input  [2:0] in_7,
  input  [2:0] in_8,
  input  [7:0] in_9,
  output [7:0] out_10
);

  wire button_1_out;

  _8bit_ALU u_8bit_alu_1 (
    .A1(in_6[0]), .B1(in_5[0]), .A2(in_6[1]), .B2(in_5[1]), .A3(in_6[2]), .B3(in_5[2]), .A4(in_6[3]),
    .B4(in_5[3]), .A5(in_6[4]), .B5(in_5[4]), .A6(in_6[5]), .B6(in_5[5]), .A7(in_6[6]), .B7(in_5[6]),
    .A8(in_6[7]), .B8(in_5[7]), .Invert_A(Invert_A), .Invert_B(Invert_B), .Select_1(Select_1),
    .Select_2(Select_2), ._8bit_output(out_10));  // open: Adder_Carry_Out, Output_A, Output_B, Output_C, Output_D, Output_A_2, Output_B_2, Output_C_2, Output_D_2
  _8Bit_Register_Bank u_8bit_register_bank_1 (
    .Sync(button_1_out), .Demux_Select(in_8), .Input(out_10), .Output(in_9), .Multiplexer_Select(in_7));
  Button button_1 (.out(button_1_out));
endmodule

module Counter (
);

  wire clock_1_out, d_ff_1_q, d_ff_1_qn, d_ff_2_q, d_ff_2_qn, d_ff_3_q, d_ff_3_qn, d_ff_4_q, d_ff_4_qn,
       d_ff_5_q, d_ff_5_qn, d_ff_6_q, d_ff_6_qn, d_ff_7_q, d_ff_7_qn, d_ff_8_qn;

  Clock clock_1 (.out(clock_1_out));
  D_Flip_Flop d_ff_1 (.clk(clock_1_out), .D(d_ff_1_qn), .Q(d_ff_1_q), .Qn(d_ff_1_qn));  // open: preset, en, reset
  LED led_1 (.in(d_ff_1_qn));
  D_Flip_Flop d_ff_2 (.clk(d_ff_1_q), .D(d_ff_2_qn), .Q(d_ff_2_q), .Qn(d_ff_2_qn));  // open: preset, en, reset
  LED led_2 (.in(d_ff_2_qn));
  D_Flip_Flop d_ff_3 (.clk(d_ff_2_q), .D(d_ff_3_qn), .Q(d_ff_3_q), .Qn(d_ff_3_qn));  // open: preset, en, reset
  LED led_3 (.in(d_ff_3_qn));
  D_Flip_Flop d_ff_4 (.clk(d_ff_3_q), .D(d_ff_4_qn), .Q(d_ff_4_q), .Qn(d_ff_4_qn));  // open: preset, en, reset
  LED led_4 (.in(d_ff_4_qn));
  D_Flip_Flop d_ff_5 (.clk(d_ff_4_q), .D(d_ff_5_qn), .Q(d_ff_5_q), .Qn(d_ff_5_qn));  // open: preset, en, reset
  LED led_5 (.in(d_ff_5_qn));
  LED led_6 (.in(d_ff_6_qn));
  D_Flip_Flop d_ff_6 (.clk(d_ff_5_q), .D(d_ff_6_qn), .Q(d_ff_6_q), .Qn(d_ff_6_qn));  // open: preset, en, reset
  LED led_7 (.in(d_ff_7_qn));
  D_Flip_Flop d_ff_7 (.clk(d_ff_6_q), .D(d_ff_7_qn), .Q(d_ff_7_q), .Qn(d_ff_7_qn));  // open: preset, en, reset
  D_Flip_Flop d_ff_8 (.clk(d_ff_7_q), .D(d_ff_8_qn), .Qn(d_ff_8_qn));  // open: Q, preset, en, reset
  LED led_8 (.in(d_ff_8_qn));
endmodule
